// Logisim project cassette player.circ as structural Verilog: 12 circuits, main circuit main
module main (
  input  Play__1___Pause__0,
  input  FF__0,
  input  Normal__stay_at_1,
  input  Pause,
  input  in_5,
  input  in_6,
  input  in_7,
  input  in_8,
  input  in_9,
  input  in_10,
  input  in_11
);

  wire _0, _1, _2, _3, _4, _5, _6, _7, and_9_out, and_10_out, button_2_out, button_out, Clock, clock_2_out,
       Dec, decoder_1_out0, decoder_1_out1, decoder_1_out2, decoder_1_out3, decoder_1_out4, decoder_1_out5,
       decoder_1_out6, decoder_1_out7, ff_1_out_4, J, OFF, OFF_Reset, ON, or_4_out, or_9_out, P, plus_1_out,
       sClock, X, Y, Z;
  wire [0:0] a;
  wire [1:1] b;
  wire [2:0] counter_5_q;
  wire [2:2] c;
  wire [3:0] counter_9_q, dH, dM, dS, H, M, S, subtractor_1_out, subtractor_2_out, subtractor_3_out,
       subtractor_4_out, subtractor_5_out, subtractor_6_out;
  wire [3:3] d;
  wire [4:4] e;
  wire [5:5] f;
  wire [6:0] a_1_out_2, a_1_out_3, a_1_out_4, a_1_out_5, a_1_out_6, a_1_out_7, a_1_out_8, i_1_out_2,
       i_1_out_3, i_1_out_4, i_1_out_5, i_1_out_6, i_1_out_7, i_1_out_8, n_1_out_2, n_1_out_3, n_1_out_4,
       n_1_out_5, n_1_out_6, n_1_out_7, n_1_out_8, o_1_out_2, o_1_out_3, o_1_out_4, o_1_out_5, o_1_out_6,
       o_1_out_7, o_1_out_8, s_1_out_2, s_1_out_3, s_1_out_4, s_1_out_5, s_1_out_6, s_1_out_7, s_1_out_8,
       t_1_out_2, t_1_out_3, t_1_out_4, t_1_out_5, t_1_out_6, t_1_out_7, t_1_out_8, t_2_out_2, t_2_out_3,
       t_2_out_4, t_2_out_5, t_2_out_6, t_2_out_7, t_2_out_8;
  wire [6:6] g;

  Button button (.out(button_out));
  Hex_Digit_Display hex_digit_display_1 (.value(subtractor_1_out));  // open: dp
  Subtractor #(.width(4)) subtractor_1 (.a(4'b1001), .b(dH), .out(subtractor_1_out));  // open: bin, bout
  DotMatrix #(.matrixcols(8), .matrixrows(8)) dotmatrix_1 (
    .col0({{7{in_5}}, a[0]}), .col1({{6{in_7}}, {2{b[1]}}}), .col2({{5{in_6}}, {3{c[2]}}}),
    .col3({{4{in_9}}, {4{d[3]}}}), .col4({{3{in_10}}, {5{e[4]}}}), .col5({{2{in_8}}, {6{f[5]}}}),
    .col6({in_11, {7{g[6]}}}), .col7({8{_7}}));
  Button button_2 (.out(button_2_out));
  or or_1 (a[0], _0, _1, _2, _3, _4, _5, _6, _7);
  or or_2 (d[3], _3, _4, _5, _6, _7);
  or or_3 (g[6], _6, _7);
  Hex_Digit_Display hex_digit_display_2 (.value(H));  // open: dp
  Hex_Digit_Display hex_digit_display_3 (.value(dH));  // open: dp
  Counter #(.width(4), .max('h9), .trigger("falling")) counter_1 (
    .Q(dH), .clk(P), .clr(OFF_Reset));  // open: load, D, count, carry
  Counter #(.width(4), .max('h9), .trigger("falling")) counter_2 (
    .Q(H), .carry(P), .clk(J), .clr(OFF_Reset));  // open: load, D, count
  Hex_Digit_Display hex_digit_display_4 (.value(subtractor_2_out));  // open: dp
  Subtractor #(.width(4)) subtractor_2 (.a(4'b1001), .b(H), .out(subtractor_2_out));  // open: bin, bout
  or or_4 (or_4_out, button_out, button_2_out);
  Hex_Digit_Display hex_digit_display_5 (.value(dM));  // open: dp
  Counter #(.width(4), .max('h5), .trigger("falling")) counter_3 (
    .Q(dM), .carry(J), .clk(Z), .clr(OFF_Reset));  // open: load, D, count
  Hex_Digit_Display hex_digit_display_6 (.value(subtractor_3_out));  // open: dp
  Subtractor #(.width(4)) subtractor_3 (.a(4'b0101), .b(dM), .out(subtractor_3_out));  // open: bin, bout
  Hex_Digit_Display hex_digit_display_7 (.value(M));  // open: dp
  Counter #(.width(4), .max('h9), .trigger("falling")) counter_4 (
    .Q(M), .carry(Z), .clk(Y), .clr(OFF_Reset));  // open: load, D, count
  Hex_Digit_Display hex_digit_display_8 (.value(subtractor_4_out));  // open: dp
  Subtractor #(.width(4)) subtractor_4 (.a(4'b1001), .b(M), .out(subtractor_4_out));  // open: bin, bout
  Decoder #(.select(3)) decoder_1 (
    .out0(decoder_1_out0), .out1(decoder_1_out1), .out2(decoder_1_out2), .out3(decoder_1_out3),
    .out4(decoder_1_out4), .out5(decoder_1_out5), .out6(decoder_1_out6), .out7(decoder_1_out7),
    .sel(counter_5_q));  // open: en
  Counter #(.width(3), .max('h7)) counter_5 (
    .load(button_out), .count(or_4_out), .Q(counter_5_q), .clk(Clock));  // open: D, carry, clr
  Hex_Digit_Display hex_digit_display_9 (.value(S));  // open: dp
  Hex_Digit_Display hex_digit_display_10 (.value(dS));  // open: dp
  Counter #(.width(4), .max('h5), .ongoal("load"), .trigger("falling")) counter_6 (
    .Q(dS), .carry(Y), .clk(X), .clr(OFF_Reset));  // open: load, D, count
  Hex_Digit_Display hex_digit_display_11 (.value(subtractor_6_out));  // open: dp
  Hex_Digit_Display hex_digit_display_12 (.value(subtractor_5_out));  // open: dp
  Subtractor #(.width(4)) subtractor_5 (.a(4'b0101), .b(dS), .out(subtractor_5_out));  // open: bin, bout
  and and_1 (_0, decoder_1_out0, ON);
  and and_2 (_7, decoder_1_out7, ON);
  or or_5 (b[1], _1, _2, _3, _4, _5, _6, _7);
  or or_6 (e[4], _4, _5, _6, _7);
  Counter #(.width(4), .max('h9), .trigger("falling")) counter_7 (
    .Q(S), .carry(X), .clk(ff_1_out_4), .clr(OFF_Reset));  // open: load, D, count
  FF ff_1 (.out_4(ff_1_out_4), .Pause(Play__1___Pause__0), .Normal(FF__0), .FF(Normal__stay_at_1));
  Subtractor #(.width(4)) subtractor_6 (.a(4'b1001), .b(S), .out(subtractor_6_out));  // open: bin, bout
  and and_3 (_1, decoder_1_out1, ON);
  and and_4 (_6, decoder_1_out6, ON);
  and and_5 (_2, decoder_1_out2, ON);
  and and_6 (_5, decoder_1_out5, ON);
  Button button_3 (.out(OFF_Reset));
  LED led_1 (.in(ON));
  Decoder decoder_2 (.out0(ON), .out1(OFF), .sel(Dec));  // open: en
  LED led_2 (.in(OFF));
  Clock clock_1 (.out(Clock));
  and and_7 (_3, decoder_1_out3, ON);
  and and_8 (_4, decoder_1_out4, ON);
  or or_7 (c[2], _2, _3, _4, _5, _6, _7);
  or or_8 (f[5], _5, _6, _7);
  Counter #(.width(1), .max('h1)) counter_8 (.count(OFF_Reset), .carry(Dec), .clk(sClock));  // open: load, D, Q, clr
  T_Flip_Flop t_ff_1 (.clk(Clock), .T(Clock), .Q(sClock), .en(Pause));  // open: Qn, preset, reset
  S s_1 (
    .out_2(s_1_out_2), .out_3(s_1_out_3), .out_4(s_1_out_4), .out_5(s_1_out_5), .out_6(s_1_out_6),
    .out_7(s_1_out_7), .out_8(s_1_out_8), .in_1(or_9_out));
  DotMatrix #(.matrixcols(7)) dotmatrix_2 (
    .col0(s_1_out_2), .col1(s_1_out_3), .col2(s_1_out_4), .col3(s_1_out_5), .col4(s_1_out_6),
    .col5(s_1_out_7), .col6(s_1_out_8));
  Clock clock_2 (.out(clock_2_out));
  Button plus_1 (.out(plus_1_out));
  T t_1 (
    .out_2(t_1_out_2), .out_3(t_1_out_3), .out_4(t_1_out_4), .out_5(t_1_out_5), .out_6(t_1_out_6),
    .out_7(t_1_out_7), .out_8(t_1_out_8), .in_1(or_9_out));
  DotMatrix #(.matrixcols(7)) dotmatrix_3 (
    .col0(t_1_out_2), .col1(t_1_out_3), .col2(t_1_out_4), .col3(t_1_out_5), .col4(t_1_out_6),
    .col5(t_1_out_7), .col6(t_1_out_8));
  and and_9 (and_9_out, OFF, clock_2_out);
  and and_10 (and_10_out, ON, plus_1_out);
  DotMatrix #(.matrixcols(7)) dotmatrix_4 (
    .col0(a_1_out_2), .col1(a_1_out_3), .col2(a_1_out_4), .col3(a_1_out_5), .col4(a_1_out_6),
    .col5(a_1_out_7), .col6(a_1_out_8));
  A a_1 (
    .out_2(a_1_out_2), .out_3(a_1_out_3), .out_4(a_1_out_4), .out_5(a_1_out_5), .out_6(a_1_out_6),
    .out_7(a_1_out_7), .out_8(a_1_out_8), .in_1(or_9_out));
  or or_9 (or_9_out, and_9_out, ON);
  Counter #(.width(4), .max('h9)) counter_9 (
    .count(and_10_out), .Q(counter_9_q), .clk(Clock), .clr(OFF));  // open: load, D, carry
  DotMatrix #(.matrixcols(7)) dotmatrix_5 (
    .col0(t_2_out_2), .col1(t_2_out_3), .col2(t_2_out_4), .col3(t_2_out_5), .col4(t_2_out_6),
    .col5(t_2_out_7), .col6(t_2_out_8));
  T t_2 (
    .out_2(t_2_out_2), .out_3(t_2_out_3), .out_4(t_2_out_4), .out_5(t_2_out_5), .out_6(t_2_out_6),
    .out_7(t_2_out_7), .out_8(t_2_out_8), .in_1(or_9_out));
  I i_1 (
    .out_2(i_1_out_2), .out_3(i_1_out_3), .out_4(i_1_out_4), .out_5(i_1_out_5), .out_6(i_1_out_6),
    .out_7(i_1_out_7), .out_8(i_1_out_8), .in_1(or_9_out));
  DotMatrix #(.matrixcols(7)) dotmatrix_6 (
    .col0(i_1_out_2), .col1(i_1_out_3), .col2(i_1_out_4), .col3(i_1_out_5), .col4(i_1_out_6),
    .col5(i_1_out_7), .col6(i_1_out_8));
  O o_1 (
    .out_2(o_1_out_2), .out_3(o_1_out_3), .out_4(o_1_out_4), .out_5(o_1_out_5), .out_6(o_1_out_6),
    .out_7(o_1_out_7), .out_8(o_1_out_8), .in_1(or_9_out));
  DotMatrix #(.matrixcols(7)) dotmatrix_7 (
    .col0(o_1_out_2), .col1(o_1_out_3), .col2(o_1_out_4), .col3(o_1_out_5), .col4(o_1_out_6),
    .col5(o_1_out_7), .col6(o_1_out_8));
  N n_1 (
    .out_2(n_1_out_2), .out_3(n_1_out_3), .out_4(n_1_out_4), .out_5(n_1_out_5), .out_6(n_1_out_6),
    .out_7(n_1_out_7), .out_8(n_1_out_8), .in_1(or_9_out));
  DotMatrix #(.matrixcols(7)) dotmatrix_8 (
    .col0(n_1_out_2), .col1(n_1_out_3), .col2(n_1_out_4), .col3(n_1_out_5), .col4(n_1_out_6),
    .col5(n_1_out_7), .col6(n_1_out_8));
  Hex_Digit_Display hex_digit_display_13 (.value(counter_9_q));  // open: dp

  // Other names for the same wires on the sheet: a[7:1] = {7{in_5}}; b (some bits) = {{6{in_7}}, b[1]};
  //   c (some bits) = {{5{in_6}}, {2{c[2]}}}; d (some bits) = {{4{in_9}}, {3{d[3]}}};
  //   e (some bits) = {{3{in_10}}, {4{e[4]}}}; f (some bits) = {{2{in_8}}, {5{f[5]}}};
  //   g (some bits) = {in_11, {6{g[6]}}}; h_t[7:0] = {8{_7}}

  // Notes on the sheet:
  //   32 Hz clock speed
  //   SIDE A
  //   SIDE B
  //   TIMER LATO A E B
  //   CONTROLLO VOLUME
  //   TIMER LATO A E B
  //   PULSANTIERA
  //   STAZIONI RADIO
endmodule

module Volume (
  input  in_1,
  input  in_2,
  input  in_3,
  input  in_4,
  input  in_5,
  input  in_6,
  input  in_7
);

  wire _0, _1, _2, _3, _4, _5, _6, _7, button_2_out, button_out, Clock, Dec, decoder_1_out0, decoder_1_out1,
       decoder_1_out2, decoder_1_out3, decoder_1_out4, decoder_1_out5, decoder_1_out6, decoder_1_out7, OFF,
       ON, or_4_out, P;
  wire [0:0] a;
  wire [1:1] b;
  wire [2:0] counter_1_q;
  wire [2:2] c;
  wire [3:3] d;
  wire [4:4] e;
  wire [5:5] f;
  wire [6:6] g;

  Button button (.out(button_out));
  DotMatrix #(.matrixcols(8), .matrixrows(8)) dotmatrix_1 (
    .col0({{7{in_1}}, a[0]}), .col1({{6{in_3}}, {2{b[1]}}}), .col2({{5{in_2}}, {3{c[2]}}}),
    .col3({{4{in_5}}, {4{d[3]}}}), .col4({{3{in_6}}, {5{e[4]}}}), .col5({{2{in_4}}, {6{f[5]}}}),
    .col6({in_7, {7{g[6]}}}), .col7({8{_7}}));
  Button button_2 (.out(button_2_out));
  or or_1 (a[0], _0, _1, _2, _3, _4, _5, _6, _7);
  or or_2 (d[3], _3, _4, _5, _6, _7);
  or or_3 (g[6], _6, _7);
  or or_4 (or_4_out, button_out, button_2_out);
  Decoder #(.select(3)) decoder_1 (
    .out0(decoder_1_out0), .out1(decoder_1_out1), .out2(decoder_1_out2), .out3(decoder_1_out3),
    .out4(decoder_1_out4), .out5(decoder_1_out5), .out6(decoder_1_out6), .out7(decoder_1_out7),
    .sel(counter_1_q));  // open: en
  Counter #(.width(3), .max('h7)) counter_1 (
    .load(button_out), .count(or_4_out), .Q(counter_1_q), .clk(Clock));  // open: D, carry, clr
  or or_5 (b[1], _1, _2, _3, _4, _5, _6, _7);
  or or_6 (e[4], _4, _5, _6, _7);
  and and_1 (_0, decoder_1_out0, ON);
  and and_2 (_7, decoder_1_out7, ON);
  and and_3 (_1, decoder_1_out1, ON);
  and and_4 (_6, decoder_1_out6, ON);
  and and_5 (_2, decoder_1_out2, ON);
  and and_6 (_5, decoder_1_out5, ON);
  and and_7 (_3, decoder_1_out3, ON);
  and and_8 (_4, decoder_1_out4, ON);
  or or_7 (c[2], _2, _3, _4, _5, _6, _7);
  or or_8 (f[5], _5, _6, _7);
  Button button_3 (.out(P));
  LED led_1 (.in(ON));
  Decoder decoder_2 (.out0(ON), .out1(OFF), .sel(Dec));  // open: en
  LED led_2 (.in(OFF));
  Clock clock_1 (.out(Clock));
  Counter counter_2 (.load(P), .carry(Dec), .clk(Clock));  // open: D, count, Q, clr

  // Other names for the same wires on the sheet: a[7:1] = {7{in_1}}; b (some bits) = {{6{in_3}}, b[1]};
  //   c (some bits) = {{5{in_2}}, {2{c[2]}}}; d (some bits) = {{4{in_5}}, {3{d[3]}}};
  //   e (some bits) = {{3{in_6}}, {4{e[4]}}}; f (some bits) = {{2{in_4}}, {5{f[5]}}};
  //   g (some bits) = {in_7, {6{g[6]}}}; h[7:0] = {8{_7}}
endmodule

module Radio (
  input  PAUSE,
  input  FF
);

  wire and_1_out, and_2_out, Clock, Dec, OFF, OFF_Reset, ON, or_1_out, Play, plus_1_out, sClock, Slowclock;
  wire [3:0] counter_1_q;
  wire [6:0] a_1_out_2, a_1_out_3, a_1_out_4, a_1_out_5, a_1_out_6, a_1_out_7, a_1_out_8, i_1_out_2,
       i_1_out_3, i_1_out_4, i_1_out_5, i_1_out_6, i_1_out_7, i_1_out_8, n_1_out_2, n_1_out_3, n_1_out_4,
       n_1_out_5, n_1_out_6, n_1_out_7, n_1_out_8, o_1_out_2, o_1_out_3, o_1_out_4, o_1_out_5, o_1_out_6,
       o_1_out_7, o_1_out_8, s_1_out_2, s_1_out_3, s_1_out_4, s_1_out_5, s_1_out_6, s_1_out_7, s_1_out_8,
       t_1_out_2, t_1_out_3, t_1_out_4, t_1_out_5, t_1_out_6, t_1_out_7, t_1_out_8, t_2_out_2, t_2_out_3,
       t_2_out_4, t_2_out_5, t_2_out_6, t_2_out_7, t_2_out_8;

  S s_1 (
    .out_2(s_1_out_2), .out_3(s_1_out_3), .out_4(s_1_out_4), .out_5(s_1_out_5), .out_6(s_1_out_6),
    .out_7(s_1_out_7), .out_8(s_1_out_8), .in_1(or_1_out));
  DotMatrix #(.matrixcols(7)) dotmatrix_1 (
    .col0(s_1_out_2), .col1(s_1_out_3), .col2(s_1_out_4), .col3(s_1_out_5), .col4(s_1_out_6),
    .col5(s_1_out_7), .col6(s_1_out_8));
  Clock clock_1 (.out(sClock));
  Button plus_1 (.out(plus_1_out));
  Button button_1 (.out(OFF_Reset));
  Decoder decoder_1 (.out0(ON), .out1(OFF), .sel(Dec));  // open: en
  DotMatrix #(.matrixcols(7)) dotmatrix_2 (
    .col0(t_1_out_2), .col1(t_1_out_3), .col2(t_1_out_4), .col3(t_1_out_5), .col4(t_1_out_6),
    .col5(t_1_out_7), .col6(t_1_out_8));
  T t_1 (
    .out_2(t_1_out_2), .out_3(t_1_out_3), .out_4(t_1_out_4), .out_5(t_1_out_5), .out_6(t_1_out_6),
    .out_7(t_1_out_7), .out_8(t_1_out_8), .in_1(or_1_out));
  and and_1 (and_1_out, OFF, sClock);
  and and_2 (and_2_out, ON, plus_1_out);
  LED led_1 (.in(ON));
  LED led_2 (.in(OFF));
  A a_1 (
    .out_2(a_1_out_2), .out_3(a_1_out_3), .out_4(a_1_out_4), .out_5(a_1_out_5), .out_6(a_1_out_6),
    .out_7(a_1_out_7), .out_8(a_1_out_8), .in_1(or_1_out));
  DotMatrix #(.matrixcols(7)) dotmatrix_3 (
    .col0(a_1_out_2), .col1(a_1_out_3), .col2(a_1_out_4), .col3(a_1_out_5), .col4(a_1_out_6),
    .col5(a_1_out_7), .col6(a_1_out_8));
  or or_1 (or_1_out, and_1_out, ON);
  Counter #(.width(4), .max('h9)) counter_1 (
    .count(and_2_out), .Q(counter_1_q), .clk(sClock), .clr(OFF));  // open: load, D, carry
  DotMatrix #(.matrixcols(7)) dotmatrix_4 (
    .col0(t_2_out_2), .col1(t_2_out_3), .col2(t_2_out_4), .col3(t_2_out_5), .col4(t_2_out_6),
    .col5(t_2_out_7), .col6(t_2_out_8));
  T t_2 (
    .out_2(t_2_out_2), .out_3(t_2_out_3), .out_4(t_2_out_4), .out_5(t_2_out_5), .out_6(t_2_out_6),
    .out_7(t_2_out_7), .out_8(t_2_out_8), .in_1(or_1_out));
  Counter counter_2 (.load(OFF_Reset), .carry(Dec), .clk(Slowclock));  // open: D, count, Q, clr
  I i_1 (
    .out_2(i_1_out_2), .out_3(i_1_out_3), .out_4(i_1_out_4), .out_5(i_1_out_5), .out_6(i_1_out_6),
    .out_7(i_1_out_7), .out_8(i_1_out_8), .in_1(or_1_out));
  DotMatrix #(.matrixcols(7)) dotmatrix_5 (
    .col0(i_1_out_2), .col1(i_1_out_3), .col2(i_1_out_4), .col3(i_1_out_5), .col4(i_1_out_6),
    .col5(i_1_out_7), .col6(i_1_out_8));
  Clock clock_2 (.out(Clock));
  DotMatrix #(.matrixcols(7)) dotmatrix_6 (
    .col0(o_1_out_2), .col1(o_1_out_3), .col2(o_1_out_4), .col3(o_1_out_5), .col4(o_1_out_6),
    .col5(o_1_out_7), .col6(o_1_out_8));
  O o_1 (
    .out_2(o_1_out_2), .out_3(o_1_out_3), .out_4(o_1_out_4), .out_5(o_1_out_5), .out_6(o_1_out_6),
    .out_7(o_1_out_7), .out_8(o_1_out_8), .in_1(or_1_out));
  and and_3 (Play, PAUSE, Slowclock);
  T_Flip_Flop t_ff_1 (.clk(Clock), .T(FF), .Qn(Slowclock));  // open: Q, preset, reset, en
  DotMatrix #(.matrixcols(7)) dotmatrix_7 (
    .col0(n_1_out_2), .col1(n_1_out_3), .col2(n_1_out_4), .col3(n_1_out_5), .col4(n_1_out_6),
    .col5(n_1_out_7), .col6(n_1_out_8));
  N n_1 (
    .out_2(n_1_out_2), .out_3(n_1_out_3), .out_4(n_1_out_4), .out_5(n_1_out_5), .out_6(n_1_out_6),
    .out_7(n_1_out_7), .out_8(n_1_out_8), .in_1(or_1_out));
  Hex_Digit_Display hex_digit_display_1 (.value(counter_1_q));  // open: dp
endmodule

module S (
  input  in_1,
  output [6:0] out_2,
  output [6:0] out_3,
  output [6:0] out_4,
  output [6:0] out_5,
  output [6:0] out_6,
  output [6:0] out_7,
  output [6:0] out_8
);

  Multiplexer #(.width(7)) multiplexer_1 (.in0({7{1'b0}}), .in1({7{1'b0}}), .out(out_2), .sel(in_1));  // open: en
  Multiplexer #(.width(7)) multiplexer_2 (.in0({7{1'b0}}), .in1(7'b0011101), .out(out_3), .sel(in_1));  // open: en
  Multiplexer #(.width(7)) multiplexer_3 (.in0({7{1'b0}}), .in1(7'b0010101), .out(out_4), .sel(in_1));  // open: en
  Multiplexer #(.width(7)) multiplexer_4 (.in0({7{1'b0}}), .in1(7'b0010101), .out(out_5), .sel(in_1));  // open: en
  Multiplexer #(.width(7)) multiplexer_5 (.in0({7{1'b0}}), .in1(7'b0010101), .out(out_6), .sel(in_1));  // open: en
  Multiplexer #(.width(7)) multiplexer_6 (.in0({7{1'b0}}), .in1(7'b0010111), .out(out_7), .sel(in_1));  // open: en
  Multiplexer #(.width(7)) multiplexer_7 (.in0({7{1'b0}}), .in1({7{1'b0}}), .out(out_8), .sel(in_1));  // open: en
endmodule

module T (
  input  in_1,
  output [6:0] out_2,
  output [6:0] out_3,
  output [6:0] out_4,
  output [6:0] out_5,
  output [6:0] out_6,
  output [6:0] out_7,
  output [6:0] out_8
);

  Multiplexer #(.width(7)) multiplexer_1 (.in0({7{1'b0}}), .in1({7{1'b0}}), .out(out_2), .sel(in_1));  // open: en
  Multiplexer #(.width(7)) multiplexer_2 (.in0({7{1'b0}}), .in1(7'b0010000), .out(out_3), .sel(in_1));  // open: en
  Multiplexer #(.width(7)) multiplexer_3 (.in0({7{1'b0}}), .in1(7'b0010000), .out(out_4), .sel(in_1));  // open: en
  Multiplexer #(.width(7)) multiplexer_4 (.in0({7{1'b0}}), .in1(7'b0011111), .out(out_5), .sel(in_1));  // open: en
  Multiplexer #(.width(7)) multiplexer_5 (.in0({7{1'b0}}), .in1(7'b0010000), .out(out_6), .sel(in_1));  // open: en
  Multiplexer #(.width(7)) multiplexer_6 (.in0({7{1'b0}}), .in1(7'b0010000), .out(out_7), .sel(in_1));  // open: en
  Multiplexer #(.width(7)) multiplexer_7 (.in0({7{1'b0}}), .in1({7{1'b0}}), .out(out_8), .sel(in_1));  // open: en
endmodule

module A (
  input  in_1,
  output [6:0] out_2,
  output [6:0] out_3,
  output [6:0] out_4,
  output [6:0] out_5,
  output [6:0] out_6,
  output [6:0] out_7,
  output [6:0] out_8
);

  Multiplexer #(.width(7)) multiplexer_1 (.in0({7{1'b0}}), .in1({7{1'b0}}), .out(out_2), .sel(in_1));  // open: en
  Multiplexer #(.width(7)) multiplexer_2 (.in0({7{1'b0}}), .in1(7'b0011111), .out(out_3), .sel(in_1));  // open: en
  Multiplexer #(.width(7)) multiplexer_3 (.in0({7{1'b0}}), .in1(7'b0010100), .out(out_4), .sel(in_1));  // open: en
  Multiplexer #(.width(7)) multiplexer_4 (.in0({7{1'b0}}), .in1(7'b0010100), .out(out_5), .sel(in_1));  // open: en
  Multiplexer #(.width(7)) multiplexer_5 (.in0({7{1'b0}}), .in1(7'b0010100), .out(out_6), .sel(in_1));  // open: en
  Multiplexer #(.width(7)) multiplexer_6 (.in0({7{1'b0}}), .in1(7'b0011111), .out(out_7), .sel(in_1));  // open: en
  Multiplexer #(.width(7)) multiplexer_7 (.in0({7{1'b0}}), .in1({7{1'b0}}), .out(out_8), .sel(in_1));  // open: en
endmodule

module I (
  input  in_1,
  output [6:0] out_2,
  output [6:0] out_3,
  output [6:0] out_4,
  output [6:0] out_5,
  output [6:0] out_6,
  output [6:0] out_7,
  output [6:0] out_8
);

  Multiplexer #(.width(7)) multiplexer_1 (.in0({7{1'b0}}), .in1({7{1'b0}}), .out(out_2), .sel(in_1));  // open: en
  Multiplexer #(.width(7)) multiplexer_2 (.in0({7{1'b0}}), .in1({7{1'b0}}), .out(out_3), .sel(in_1));  // open: en
  Multiplexer #(.width(7)) multiplexer_3 (.in0({7{1'b0}}), .in1({7{1'b0}}), .out(out_4), .sel(in_1));  // open: en
  Multiplexer #(.width(7)) multiplexer_4 (.in0({7{1'b0}}), .in1(7'b0011111), .out(out_5), .sel(in_1));  // open: en
  Multiplexer #(.width(7)) multiplexer_5 (.in0({7{1'b0}}), .in1({7{1'b0}}), .out(out_6), .sel(in_1));  // open: en
  Multiplexer #(.width(7)) multiplexer_6 (.in0({7{1'b0}}), .in1({7{1'b0}}), .out(out_7), .sel(in_1));  // open: en
  Multiplexer #(.width(7)) multiplexer_7 (.in0({7{1'b0}}), .in1({7{1'b0}}), .out(out_8), .sel(in_1));  // open: en
endmodule

module O (
  input  in_1,
  output [6:0] out_2,
  output [6:0] out_3,
  output [6:0] out_4,
  output [6:0] out_5,
  output [6:0] out_6,
  output [6:0] out_7,
  output [6:0] out_8
);

  Multiplexer #(.width(7)) multiplexer_1 (.in0({7{1'b0}}), .in1({7{1'b0}}), .out(out_2), .sel(in_1));  // open: en
  Multiplexer #(.width(7)) multiplexer_2 (.in0({7{1'b0}}), .in1(7'b0011111), .out(out_3), .sel(in_1));  // open: en
  Multiplexer #(.width(7)) multiplexer_3 (.in0({7{1'b0}}), .in1(7'b0010001), .out(out_4), .sel(in_1));  // open: en
  Multiplexer #(.width(7)) multiplexer_4 (.in0({7{1'b0}}), .in1(7'b0010001), .out(out_5), .sel(in_1));  // open: en
  Multiplexer #(.width(7)) multiplexer_5 (.in0({7{1'b0}}), .in1(7'b0010001), .out(out_6), .sel(in_1));  // open: en
  Multiplexer #(.width(7)) multiplexer_6 (.in0({7{1'b0}}), .in1(7'b0011111), .out(out_7), .sel(in_1));  // open: en
  Multiplexer #(.width(7)) multiplexer_7 (.in0({7{1'b0}}), .in1({7{1'b0}}), .out(out_8), .sel(in_1));  // open: en
endmodule

module N (
  input  in_1,
  output [6:0] out_2,
  output [6:0] out_3,
  output [6:0] out_4,
  output [6:0] out_5,
  output [6:0] out_6,
  output [6:0] out_7,
  output [6:0] out_8
);

  Multiplexer #(.width(7)) multiplexer_1 (.in0({7{1'b0}}), .in1({7{1'b0}}), .out(out_2), .sel(in_1));  // open: en
  Multiplexer #(.width(7)) multiplexer_2 (.in0({7{1'b0}}), .in1(7'b0011111), .out(out_3), .sel(in_1));  // open: en
  Multiplexer #(.width(7)) multiplexer_3 (.in0({7{1'b0}}), .in1(7'b0001000), .out(out_4), .sel(in_1));  // open: en
  Multiplexer #(.width(7)) multiplexer_4 (.in0({7{1'b0}}), .in1(7'b0000100), .out(out_5), .sel(in_1));  // open: en
  Multiplexer #(.width(7)) multiplexer_5 (.in0({7{1'b0}}), .in1(7'b0000010), .out(out_6), .sel(in_1));  // open: en
  Multiplexer #(.width(7)) multiplexer_6 (.in0({7{1'b0}}), .in1(7'b0011111), .out(out_7), .sel(in_1));  // open: en
  Multiplexer #(.width(7)) multiplexer_7 (.in0({7{1'b0}}), .in1({7{1'b0}}), .out(out_8), .sel(in_1));  // open: en
endmodule

module FF (
  input  Normal,
  input  FF,
  input  Pause,
  output out_4
);

  wire clock_1_out, t_ff_1_q, t_ff_2_q, t_ff_3_q, t_ff_4_q;

  Clock clock_1 (.out(clock_1_out));
  T_Flip_Flop t_ff_1 (.clk(clock_1_out), .T(clock_1_out), .Q(t_ff_1_q), .en(Pause));  // open: Qn, preset, reset
  T_Flip_Flop t_ff_2 (.clk(t_ff_1_q), .T(t_ff_1_q), .Q(t_ff_2_q));  // open: Qn, preset, reset, en
  T_Flip_Flop t_ff_3 (.clk(t_ff_2_q), .T(t_ff_2_q), .Q(t_ff_3_q));  // open: Qn, preset, reset, en
  T_Flip_Flop t_ff_4 (.clk(t_ff_3_q), .T(t_ff_3_q), .Q(t_ff_4_q));  // open: Qn, preset, reset, en
  Multiplexer multiplexer_1 (.in0(clock_1_out), .in1(t_ff_4_q), .out(out_4), .sel(Normal), .en(FF));
endmodule

module Play_Circuit (
  input  Pause
);

  wire Clock, Dec, OFF, OFF_Reset, ON, sClock;

  Button button_1 (.out(OFF_Reset));
  Clock clock_1 (.out(Clock));
  LED led_1 (.in(ON));
  Decoder decoder_1 (.out0(ON), .out1(OFF), .sel(Dec));  // open: en
  LED led_2 (.in(OFF));
  T_Flip_Flop t_ff_1 (.clk(Clock), .T(Clock), .Q(sClock), .en(Pause));  // open: Qn, preset, reset
  Counter #(.width(1), .max('h1)) counter_1 (.count(OFF_Reset), .carry(Dec), .clk(sClock));  // open: load, D, Q, clr
endmodule

module Sides (
  input  Play__1___Pause__0,
  input  FF__0,
  input  Normal__stay_at_1,
  input  Pause
);

  wire Clock, Dec, ff_1_out_4, J, OFF, OFF_Reset, ON, P, sClock, X, Y, Z;
  wire [3:0] dH, dM, dS, H, M, S, subtractor_1_out, subtractor_2_out, subtractor_3_out, subtractor_4_out,
       subtractor_5_out, subtractor_6_out;

  Subtractor #(.width(4)) subtractor_1 (.a(4'b1001), .b(dH), .out(subtractor_1_out));  // open: bin, bout
  Hex_Digit_Display hex_digit_display_1 (.value(dH));  // open: dp
  Counter #(.width(4), .max('h9), .trigger("falling")) counter_1 (
    .Q(dH), .clk(P), .clr(OFF_Reset));  // open: load, D, count, carry
  Hex_Digit_Display hex_digit_display_2 (.value(subtractor_1_out));  // open: dp
  Subtractor #(.width(4)) subtractor_2 (.a(4'b1001), .b(H), .out(subtractor_2_out));  // open: bin, bout
  Hex_Digit_Display hex_digit_display_3 (.value(H));  // open: dp
  Counter #(.width(4), .max('h9), .trigger("falling")) counter_2 (
    .Q(H), .carry(P), .clk(J), .clr(OFF_Reset));  // open: load, D, count
  Hex_Digit_Display hex_digit_display_4 (.value(subtractor_2_out));  // open: dp
  Hex_Digit_Display hex_digit_display_5 (.value(dM));  // open: dp
  Hex_Digit_Display hex_digit_display_6 (.value(M));  // open: dp
  Counter #(.width(4), .max('h5), .trigger("falling")) counter_3 (
    .Q(dM), .carry(J), .clk(Z), .clr(OFF_Reset));  // open: load, D, count
  Hex_Digit_Display hex_digit_display_7 (.value(subtractor_3_out));  // open: dp
  Hex_Digit_Display hex_digit_display_8 (.value(subtractor_4_out));  // open: dp
  Subtractor #(.width(4)) subtractor_3 (.a(4'b1001), .b(M), .out(subtractor_3_out));  // open: bin, bout
  Subtractor #(.width(4)) subtractor_4 (.a(4'b0101), .b(dM), .out(subtractor_4_out));  // open: bin, bout
  Hex_Digit_Display hex_digit_display_9 (.value(dS));  // open: dp
  Counter #(.width(4), .max('h5), .ongoal("load"), .trigger("falling")) counter_4 (
    .Q(dS), .carry(Y), .clk(X), .clr(OFF_Reset));  // open: load, D, count
  Counter #(.width(4), .max('h9), .trigger("falling")) counter_5 (
    .Q(M), .carry(Z), .clk(Y), .clr(OFF_Reset));  // open: load, D, count
  Hex_Digit_Display hex_digit_display_10 (.value(subtractor_6_out));  // open: dp
  Hex_Digit_Display hex_digit_display_11 (.value(S));  // open: dp
  Counter #(.width(4), .max('h9), .trigger("falling")) counter_6 (
    .Q(S), .carry(X), .clk(ff_1_out_4), .clr(OFF_Reset));  // open: load, D, count
  Hex_Digit_Display hex_digit_display_12 (.value(subtractor_5_out));  // open: dp
  Subtractor #(.width(4)) subtractor_5 (.a(4'b1001), .b(S), .out(subtractor_5_out));  // open: bin, bout
  Subtractor #(.width(4)) subtractor_6 (.a(4'b0101), .b(dS), .out(subtractor_6_out));  // open: bin, bout
  FF ff_1 (.out_4(ff_1_out_4), .Pause(Play__1___Pause__0), .Normal(FF__0), .FF(Normal__stay_at_1));
  Button button_1 (.out(OFF_Reset));
  Decoder decoder_1 (.out0(ON), .out1(OFF), .sel(Dec));  // open: en
  Clock clock_1 (.out(Clock));
  LED led_1 (.in(ON));
  LED led_2 (.in(OFF));
  T_Flip_Flop t_ff_1 (.clk(Clock), .T(Clock), .Q(sClock), .en(Pause));  // open: Qn, preset, reset
  Counter #(.width(1), .max('h1)) counter_7 (.count(OFF_Reset), .carry(Dec), .clk(sClock));  // open: load, D, Q, clr

  // Notes on the sheet:
  //   64 Hz clock speed
  //   SIDE A
  //   SIDE B
endmodule
